# Fritzing sketch Esquematico (saved by Fritzing 0.9.4)
breadboards: 1

parts:
  R1 = Resistor [tolerance=±5% resistance=220 package=THT]
  R2 = Resistor [tolerance=±5% resistance=220 package=THT]
  R3 = Resistor [tolerance=±5% resistance=220 package=THT]
  R4 = Resistor [tolerance=±5% resistance=220 package=THT]
  R5 = Resistor [tolerance=±5% resistance=220 package=THT]
  R6 = Resistor [tolerance=±5% resistance=220 package=THT]
  LED1 = LED - 5mm [color="Red (633nm)" package="5 mm [THT]"]
  LED2 = LED - 5mm [color="Red (633nm)" package="5 mm [THT]"]
  LED3 = LED - 5mm [color="Red (633nm)" package="5 mm [THT]"]
  LED4 = LED - 5mm [color="Red (633nm)" package="5 mm [THT]"]
  LED5 = LED - 5mm [color="Red (633nm)" package="5 mm [THT]"]
  LED6 = LED - 5mm [color="Red (633nm)" package="5 mm [THT]"]
  Componente1 = Arduino Uno (Rev3) - ICSP

nets:
  N1: R1.Pin_0, LED1.cathode
  N2: R1.Pin_1, R2.Pin_1, R3.Pin_1, R4.Pin_1, R5.Pin_1, R6.Pin_1, Componente1.GND
  N3: R2.Pin_0, LED2.cathode
  N4: R3.Pin_0, LED3.cathode
  N5: R4.Pin_0, LED4.cathode
  N6: R5.Pin_0, LED5.cathode
  N7: R6.Pin_0, LED6.cathode
  N8: LED1.anode, Componente1.D13/SCK
  N9: LED2.anode, Componente1.D12/MISO
  N10: LED3.anode, Componente1.D11_PWM/MOSI
  N11: LED4.anode, Componente1.D10_PWM/SS
  N12: LED5.anode, Componente1.D9_PWM
  N13: LED6.anode, Componente1.D8
